// Digital circuit addr_decoder.dig as structural Verilog
module addr_decoder (
  input  nMREQ,
  input  A15,
  output RAMnEN___8000__FFFF,
  output ROMnEN___0000__7FFF
);

  wire nand_1_out, nand_2_out;

  nand nand_1 (nand_1_out, nMREQ, nMREQ);
  nand nand_2 (nand_2_out, A15, A15);
  nand nand_3 (RAMnEN___8000__FFFF, nand_1_out, A15);
  nand nand_4 (ROMnEN___0000__7FFF, nand_1_out, nand_2_out);

  // Notes on the sheet:
  //   nMREQ: default 1
endmodule
